# Fritzing sketch Circuit (saved by Fritzing 0.9.10b)
breadboards: 1

parts:
  Mod1 = Raspberry Pi Pico
  R1 = Resistor [tolerance=±5% power=0.25 resistance=330 package=THT]
  Q1 = NPN-Transistor [package="TO92 [THT]"]
  R2 = Resistor [tolerance=±5% power=0.25 resistance=1k package=THT]
  Q2 = MOSFET-NCHANNEL [package=to-92]
  M1 = DC Motor [voltage_(max)=6V voltage_(min)=3V]
  D1 = Rectifier Diode 10A [part_number=P1000K]
  U1 = LM393 [package=so08]
  R3 = Resistor [tolerance=±20% power=0.25 resistance=100k package=THT]
  R4 = Resistor [tolerance=±20% power=0.25 resistance=100k package=THT]
  R5 = Resistor [tolerance=±20% power=0.25 resistance=100k package=THT]
  R6 = Resistor [tolerance=±20% power=0.25 resistance=1M package=THT]
  R7 = Resistor [tolerance=±20% power=0.25 resistance=3.3k package=THT]
  C1 = Electrolytic Capacitor [capacitance=1µF voltage=35V package="100 mil [THT, electrolytic]"]

nets:
  GND: Mod1.pin_3, Mod1.pin_28, Q1.E, M1.pin_2, D1.anode, U1.G1_V-, R4.Pin_0, C1.-
  N1: Mod1.pin_19, R1.Pin_0
  N2: Mod1.pin_24, U1.G1_OUT, R5.Pin_0, R6.Pin_0, R7.Pin_0
  N3: Mod1.pin_36, U1.G1_V+, R3.Pin_1, R7.Pin_1
  N4: R1.Pin_1, Q1.B
  N5: Q1.C, R2.Pin_1, Q2.G
  12V: R2.Pin_0, Q2.D
  N6: Q2.S, M1.pin_1, D1.cathode
  N7: U1.G1_-IN, R6.Pin_1, C1.+
  N8: U1.G1_+IN, R4.Pin_1
  N9: R3.Pin_0, R5.Pin_1

custom parts:
  Raspberry Pi Pico: Raspberry Pi Pico. Based around the RP2040 microcontroller the Pico is a low cost microcontroller device bringing Raspberry Pi quality, cost, and easy of use to the microcontroller space. Jan 2021, Split part in to two versions: tht (this one) and SMD. This one will drill holes for a .1 in header in pcb to allow plugging in the module as well as providing pads to solder the module to the top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
